# Fritzing sketch schematic (saved by Fritzing 0.9.3b)

parts:
  LCD1 = LCD screen
  Raspberry_Pi_1 = Raspberry Pi 4 [part_number=RPI-4-b]
  LCM1602_IIC1 = LCM1602 IIC [part_number="LCM1602 IIC" chip_label="LCM1602 IIC" package="DIP (Dual Inline) [THT]"]
  U1 = LIPO-2000mAh [package=lipo-2000]
  SP1 = SPEAKER [package=pcb_mount_speaker]
  LED1 = LEDs [package=led10mm]
  USB_MICROPHONE = USB connector [package=THT]  # not connected

nets:
  VSS: LCD1.VSS, LCM1602_IIC1.VSS
  VDD: LCD1.VDD, LCM1602_IIC1.VDD
  N1: LCD1.V0, LCM1602_IIC1.V0
  N2: LCD1.RS, LCM1602_IIC1.RS
  N3: LCD1.R/W, LCM1602_IIC1.RW
  N4: LCD1.E, LCM1602_IIC1.E
  N5: LCD1.DB0, LCM1602_IIC1.D0
  N6: LCD1.DB1, LCM1602_IIC1.D1
  N7: LCD1.DB2, LCM1602_IIC1.D2
  N8: LCD1.DB3, LCM1602_IIC1.D3
  N9: LCD1.DB4, LCM1602_IIC1.D4
  N10: LCD1.DB5, LCM1602_IIC1.D5
  N11: LCD1.DB6, LCM1602_IIC1.D6
  N12: LCD1.DB7, LCM1602_IIC1.D7
  N13: LCD1.LED+, LCM1602_IIC1.A
  N14: LCD1.LED-, LCM1602_IIC1.K
  N15: Raspberry_Pi_1.GPIO2, LCM1602_IIC1.SDA
  N16: Raspberry_Pi_1.GPIO3, LCM1602_IIC1.SCL
  N17: Raspberry_Pi_1.GPIO4, SP1.-
  GND: Raspberry_Pi_1.GND, LCM1602_IIC1.GND, U1.-, SP1.+, LED1.C
  N18: Raspberry_Pi_1.GPIO15, LED1.A
  5V: Raspberry_Pi_1.5V, LCM1602_IIC1.VCC
  N19: LCM1602_IIC1.LED_A, LCM1602_IIC1.LED_B

custom parts:
  Raspberry Pi 4: The RPi4, a faster version of the awesome Raspberry Pi 2 B ARM Board with 40 pin gpio. Ready for special Raspberry Pi B+ and RPi2 Hat (Hardware attached (on) top)
  LCM1602 IIC: I2C-Module to use a 1602 or 2004 LCD on with the wire.h libory Serial LCD Modul
